// Logisim project cpu.circ as structural Verilog: 7 circuits, main circuit main
module main (
);

  wire ALU_A_IN, ALU_A_OUT, ALU_B_IN, ALU_B_OUT, alu_carry, ALU_HIGH, ALU_LATCH, ALU_OUT, alu_zero,
       and_1_out, and_2_out, button_1_out, button_2_out, button_3_out, button_4_out, clk, CONST_0_OUT,
       CONST_1_OUT, CONST_7_OUT, DONE_FETCH, keep, microcode_overflow, MICROCODE_RESET, OPCODE_IN, or_1_out,
       or_2_out, or_3_out, PC_HIGH, PC_IN, PC_INC, PC_OUT, RAM_ADDR_HIGH, RAM_ADDR_IN, RAM_IN, RAM_OUT,
       RESET_IF_CARRY, RESET_IF_ZERO, reset_microcode, reset_opcode, ret, rst_direction, rst_inc,
       rst_overflow, rst_read, rst_write, short, STACK_IN, STACK_OUT, STACK_SWAP, wst_direction, wst_inc,
       wst_overflow, wst_read, wst_write, xor_1_out;
  wire [1:0] STACK_INC;
  wire [2:0] ALU_CMD;
  wire [3:0] microcode_counter_q;
  wire [4:0] opcode;
  wire [7:0] A_q, alu_1_q, B_q, data_bus, program_counter_1_q, ram_1_dout;
  wire [10:0] register_1_q;
  wire [15:0] A_q16, B_q16, ram_addr;
  wire [31:5] Microcode_ROM_data;

  Clock clock_1 (.out(clk));
  Counter #(.max('hf), .width(4)) microcode_counter (
    .D(4'b0000), .count(1'b1), .Q(microcode_counter_q), .carry(microcode_overflow), .up(1'b1), .clk(clk),
    .clr(reset_microcode));  // open: load
  // Probe on ALU_CMD
  // Probe on STACK_INC
  xor xor_1 (xor_1_out, ret, STACK_SWAP);
  Button button_1 (.out(button_1_out));
  Demultiplexer #(.width(4)) demultiplexer_1 (
    .out0({wst_write, wst_read, wst_direction, wst_inc}),
    .out1({rst_write, rst_read, rst_direction, rst_inc}), .in({STACK_IN, STACK_OUT, STACK_INC}),
    .sel(xor_1_out));
  // Probe on {opcode, keep, short, microcode_counter_q}
  Register #(.trigger("falling"), .width(11)) register_1 (
    .D({opcode, keep, short, microcode_counter_q}), .en(1'b1), .clk(clk), .Q(register_1_q));  // open: clr
  ROM #(.addrWidth(11), .dataWidth(32)) Microcode_ROM (
    .addr(register_1_q),
    .data({Microcode_ROM_data[31:28], DONE_FETCH, RESET_IF_ZERO, RESET_IF_CARRY, MICROCODE_RESET, ALU_HIGH, ALU_LATCH, ALU_B_IN, ALU_A_IN, PC_HIGH, PC_INC, PC_IN, OPCODE_IN, RAM_ADDR_HIGH, RAM_ADDR_IN, RAM_IN, STACK_SWAP, STACK_IN, Microcode_ROM_data[10:5], STACK_INC, ALU_CMD}));
  // Probe on Microcode_ROM_data[10:6]
  Register #(.trigger("high")) current_instruction (
    .D(data_bus), .en(OPCODE_IN), .clk(OPCODE_IN), .Q({keep, ret, short, opcode}), .clr(reset_opcode));
  program_counter program_counter_1 (
    .D(data_bus), .WE(PC_IN), .BS(PC_HIGH), .INC(PC_INC), .CLK(clk), .RESET(button_1_out),
    .Q(program_counter_1_q));  // open: Q16
  // Probe on program_counter_1_q
  Decoder #(.select(5)) decoder_1 (
    .out0(STACK_OUT), .out1(RAM_OUT), .out2(PC_OUT), .out3(ALU_OUT), .out4(ALU_A_OUT), .out5(ALU_B_OUT),
    .out6(CONST_0_OUT), .out7(CONST_1_OUT), .out8(CONST_7_OUT), .sel(Microcode_ROM_data[10:6]),
    .en(Microcode_ROM_data[5]));  // open: out9, out10, out11, out12, out13, out14, out15, out16, out17, out18, out19, out20, out21, out22, out23, out24, out25, out26, out27, out28, out29, out30, out31
  and and_1 (and_1_out, RESET_IF_CARRY, alu_carry);
  and and_2 (and_2_out, RESET_IF_ZERO, alu_zero);
  Button button_2 (.out(button_2_out));
  assign data_bus = PC_OUT ? program_counter_1_q : 8'bz;  // Controlled_Buffer controlled_buffer_1
  or or_1 (or_1_out, and_1_out, and_2_out, MICROCODE_RESET, 1'b0, button_2_out);
  Hex_Digit_Display hex_digit_display_1 (.value(data_bus[7:4]));  // open: dp
  Hex_Digit_Display hex_digit_display_2 (.value(data_bus[3:0]));  // open: dp
  S_R_Flip_Flop #(.trigger("high")) s_r_ff_1 (
    .S(or_1_out), .R(button_3_out), .clk(1'b1));  // open: Q, reset, Qn, preset
  Button button_3 (.out(button_3_out));
  RAM #(.addrWidth(16), .enables("line"), .trigger("falling")) ram_1 (
    .addr(ram_addr), .we(RAM_IN), .clk(clk), .din(data_bus), .dout(ram_1_dout));
  or or_2 (or_2_out, microcode_overflow, or_1_out);
  or or_3 (or_3_out, or_1_out, OPCODE_IN);
  Button button_4 (.out(button_4_out));
  stack wst (
    .OE(wst_read), .direction(wst_direction), .WE(wst_write), .enable(wst_inc), .data_in(data_bus),
    .clk(clk), .overflow(wst_overflow), .data_out(data_bus));
  LED led_1 (.in(keep));
  LED led_2 (.in(ret));
  LED led_3 (.in(short));
  // Probe on opcode
  assign data_bus = CONST_1_OUT ? 8'h1 : 8'bz;  // Controlled_Buffer controlled_buffer_2
  assign data_bus = CONST_0_OUT ? {8{1'b0}} : 8'bz;  // Controlled_Buffer controlled_buffer_3
  assign data_bus = CONST_7_OUT ? 8'h7 : 8'bz;  // Controlled_Buffer controlled_buffer_4
  and and_3 (reset_opcode, ~clk, or_2_out);  // AND_Gate
  and and_4 (reset_microcode, ~clk, or_3_out);  // AND_Gate
  S_R_Flip_Flop #(.trigger("high")) s_r_ff_2 (
    .S(or_3_out), .R(button_4_out), .clk(1'b1));  // open: Q, reset, Qn, preset
  // Probe on ram_1_dout
  assign data_bus = RAM_OUT ? ram_1_dout : 8'bz;  // Controlled_Buffer controlled_buffer_5
  reg_8_16_8 A (.D(data_bus), .BS(ALU_HIGH), .WE(ALU_A_IN), .CLK(clk), .Q16(A_q16), .Q(A_q));
  assign data_bus = ALU_A_OUT ? A_q : 8'bz;  // Controlled_Buffer controlled_buffer_6
  reg_8_16_8 B (.D(data_bus), .BS(ALU_HIGH), .WE(ALU_B_IN), .CLK(clk), .Q16(B_q16), .Q(B_q));
  assign data_bus = ALU_B_OUT ? B_q : 8'bz;  // Controlled_Buffer controlled_buffer_7
  stack rst (
    .OE(rst_read), .direction(rst_direction), .WE(rst_write), .enable(rst_inc), .data_in(data_bus),
    .clk(clk), .overflow(rst_overflow), .data_out(data_bus));
  reg_8_16_8 u_RAM_ADDR (.D(data_bus), .BS(RAM_ADDR_HIGH), .WE(RAM_ADDR_IN), .CLK(clk), .Q16(ram_addr));  // open: Q
  // Probe on ram_addr
  alu alu_1 (
    .WE(ALU_LATCH), .A(A_q16), .B(B_q16), .BS(ALU_HIGH), .CMD(ALU_CMD), .CLK(clk), .Q(alu_1_q), .Z(alu_zero),
    .C(alu_carry));
  assign data_bus = ALU_OUT ? alu_1_q : 8'bz;  // Controlled_Buffer controlled_buffer_8

  // Notes on the sheet:
  //   Choose which stack to operate on
  //   contents of Microcode_ROM (hex, n*v repeats v):
  //   40a0 8c0a0 50060 13*0 40a8 8c0a0 40868 40a0 8c0a0 40860 1000000 9*0 40a8 8c0a0 1040860 13*0 40a8
  //   8c0a0 40868 40a0 8c0a0 40860 1000000 9*0 100020 2001e0 14008e0 13*0 100038 900020 a001a0 2001e0
  //   8008e8 10008e0 10*0 100028 2001e0 10008e0 13*0 100038 900028 a001a8 2001e0 8008e8 10008e0 10*0
  //   1000018 15*0 18 1000018 14*0 1000000 15*0 1000000 15*0 100028 1000920 14*0 100038 900028 8 800928
  //   1000920 11*0 100028 928 1000920 29*0 100038 1000920 14*0 100038 900038 938 1800928 12*0 100028
  //   1000920 14*0 100038 900028 8 800928 1000920 11*0 100038 200020 928 1000960 12*0 100038 900038 200038
  //   a00020 800928 928 800968 1000960 8*0 100038 200028 8 928 1000960 11*0 100038 900038 200038 a00028 8
  //   8 8 800928 928 800968 1000960 5*0 18 100028 8 920 1000000 11*0 18 18 100038 900028 8 8 8 800928 920
  //   1000000 6*0 100038 900028 8 800928 928 1800920 10*0 100038 900038 200038 a00028 8 8 8 800928 928
  //   800968 968 800928 1000920 0 0 0 100038 900038 200020 800928 928 1000960 10*0 100038 900038 200038
  //   e0003e 100038 900020 8008e8 8e8 6*8 0 0 100038 900038 200028 8 8 800928 928 1000960 24*0 b001a0
  //   100038 600021 9e0 4000000 9a0 1000000 9*0 100038 900038 200038 e00021 9e0 4000000 9a0 1000000 8*0
  //   b001a0 100038 600029 8 9e0 4000000 9a0 1000000 8*0 100038 900038 200038 e00029 8 8 8 9e0 4000000 9a0
  //   1000000 197*0 b001a0 100020 600227 1001a0 6000e1 9000e0 100020 a800b8 6000a0 200e0 18a00e0 5*0 20038
  //   10a0038 14*0 b001a0 100020 600227 1001a0 6000e1 9000e0 100020 a800a0 6000a0 200e0 18a00e0 5*0 20038
  //   a0028 1000008 13*0 b001a0 100038 6001e1 100038 4000000 60022f 1001a0 6000e1 9000e0 100038 2000a0
  //   e800a0 200e0 18a00e0 0 0 b001a0 100038 6001f9 18 4000000 8 a0028 20038 1000018 7*0 b001a0 100038
  //   6001e1 100028 4000000 60023f 1001a0 6000e1 9000e0 100028 2000a0 e800a0 200e0 18a00e0 0 0 b001a0
  //   100038 6001e9 4000000 18 20038 a0028 8 1000000 7*0 b001a0 100020 600227 1001a0 6000e1 9000e0 100020
  //   a800b8 6000a0 1008 8a18e8 10218e0 4*0 20038 a0038 1008 818a8 10018a0 11*0 b001a0 100020 600227
  //   1001a0 6000e1 9000e0 100020 a800a0 6000a0 1008 8a18e8 10218e0 4*0 20038 a0028 1008 818a8 10018a0
  //   11*0 100038 1008 1920 1000000 12*0 100038 900038 1008 1928 801920 1000000 10*0 100020 1008 1920
  //   1000000 12*0 100038 900028 1008 1928 801920 1000000 10*0 c1a0 4020 860 1000000 12*0 b0c1a0 104020
  //   868 6001e0 40e0 80c0e0 860 9*0 c1a0 4028 860 1000000 12*0 b0c1a0 104028 868 6001e0 40e0 80c0e0 860
  //   9*0 c1a0 4038 1002038 13*0 104038 b0c1b8 2028 6001e0 40e0 80c0e0 2038 1000018 8*0 c1a0 4038 1002028
  //   13*0 104038 b0c1b8 2028 6001e0 40e0 80c0e0 2028 1000008 392*0 100038 200020 14008e0 13*0 100038
  //   900038 200038 e00020 8008e8 10008e0 10*0 100038 200028 400008 10008e0 12*0 100038 900038 200038
  //   e00028 8 8 8 8008e8 10008e0 7*0 100038 200020 4008e1 13*0 100038 900038 200038 e00021 8008e8 8e0
  //   10*0 100038 200028 400009 8e0 12*0 100038 900038 200038 e00029 8 8 8 8008e8 8e0 7*0 100038 200020
  //   4008e2 13*0 100038 900038 200038 e00022 8008e8 8e0 10*0 100038 200028 40000a 8e0 12*0 100038 900038
  //   200038 e0002a 8 8 8 8008e8 8e0 7*0 100038 200020 4008e3 13*0 100038 900038 200038 e00023 8008e8 8e0
  //   10*0 100038 200028 40000b 8e0 12*0 100038 900038 200038 e0002b 8 8 8 8008e8 8e0 7*0 100038 200020
  //   4008e4 13*0 100038 900038 200038 e00024 8008e8 8e0 10*0 100038 200028 40000c 8e0 12*0 100038 900038
  //   200038 e0002c 8 8 8 8008e8 8e0 7*0 100038 200020 4008e5 13*0 100038 900038 200038 e00025 8008e8 8e0
  //   10*0 100038 200028 40000d 8e0 12*0 100038 900038 200038 e0002d 8 8 8 8008e8 8e0 7*0 100038 200020
  //   4008e6 13*0 100038 900038 200038 e00026 8008e8 8e0 10*0 100038 200028 40000e 8e0 12*0 100038 900038
  //   200038 e0002e 8 8 8 8008e8 8e0
  //   Microcode jump circuit
endmodule

module stack (
  input  OE,
  input  direction,
  input  WE,
  input  enable,
  input  [7:0] data_in,
  input  clk,
  output overflow,
  output [7:0] data_out
);

  wire not_1_out;
  wire [7:0] wst_dout, wst_head_q;

  Counter #(.ongoal("stay"), .trigger("falling")) wst_head (
    .clr(1'b0), .load(1'b0), .up(not_1_out), .count(enable), .clk(clk), .carry(overflow), .Q(wst_head_q));  // open: D
  not not_1 (not_1_out, direction);
  RAM #(.enables("line"), .trigger("falling")) wst (
    .addr(wst_head_q), .we(WE), .clk(clk), .din(data_in), .dout(wst_dout));
  assign data_out = OE ? wst_dout : 8'bz;  // Controlled_Buffer controlled_buffer_1

  // Other names for the same wires on the sheet: load = OE

  // Notes on the sheet:
  //   direction: pull=up
  //   enable: pull=down
  //   WE: pull=down
  //   OE: pull=down
endmodule

module reg_8_16_8 (
  input  [7:0] D,
  input  BS,
  input  WE,
  input  CLK,
  output [15:0] Q16,
  output [7:0] Q
);

  wire [3:0] multiplexer_1_out;
  wire [15:0] and_1_out, D16, multiplexer_2_out, shifter_1_out;

  Multiplexer #(.width(4)) multiplexer_1 (.in0(4'b1000), .in1(4'b0000), .out(multiplexer_1_out), .sel(BS));
  Multiplexer #(.width(16)) multiplexer_2 (.in0(16'hff00), .in1(16'hff), .out(multiplexer_2_out), .sel(BS));
  Register #(.width(16)) register_1 (.D(D16), .en(WE), .clk(CLK), .Q(Q16));  // open: clr
  Shifter #(.shift("lr"), .width(16)) shifter_1 (.in({D, {8{1'b0}}}), .\dist (multiplexer_1_out), .out(shifter_1_out));
  assign and_1_out = multiplexer_2_out & Q16;  // AND_Gate and_1, 16 bits wide
  assign D16 = shifter_1_out | and_1_out;  // OR_Gate or_1, 16 bits wide
  Multiplexer #(.width(8)) multiplexer_3 (.in0(Q16[7:0]), .in1(Q16[15:8]), .out(Q), .sel(BS));

  // Other names for the same wires on the sheet: D8[7:0] = D; high = BS; Q8[7:0] = Q
endmodule

module test_reg (
);

  wire button_1_out, dipswitch_1_sw1, dipswitch_1_sw2, dipswitch_1_sw8;
  wire [7:0] reg_8_16_8_1_q;
  wire [15:0] reg_8_16_8_1_q16;

  DipSwitch dipswitch_1 (
    .sw1(dipswitch_1_sw1), .sw2(dipswitch_1_sw2), .sw8(dipswitch_1_sw8));  // open: sw3, sw4, sw5, sw6, sw7
  Button button_1 (.out(button_1_out));
  reg_8_16_8 reg_8_16_8_1 (
    .D(8'he), .BS(dipswitch_1_sw1), .WE(dipswitch_1_sw2), .CLK(button_1_out), .Q16(reg_8_16_8_1_q16),
    .Q(reg_8_16_8_1_q));
  // Probe on reg_8_16_8_1_q16
  // Probe on reg_8_16_8_1_q
endmodule

module program_counter (
  input  [7:0] D,
  input  WE,
  input  BS,
  input  INC,
  input  CLK,
  input  RESET,
  output [15:0] Q16,
  output [7:0] Q
);

  wire [3:0] multiplexer_1_out;
  wire [15:0] and_1_out, D16, multiplexer_2_out, shifter_1_out;

  Multiplexer #(.width(4)) multiplexer_1 (.in0(4'b1000), .in1(4'b0000), .out(multiplexer_1_out), .sel(BS));
  Multiplexer #(.width(16)) multiplexer_2 (.in0(16'hff00), .in1(16'hff), .out(multiplexer_2_out), .sel(BS));
  Counter #(.max('hffff), .trigger("falling"), .width(16)) counter_1 (
    .load(WE), .D(D16), .count(INC), .Q(Q16), .up(1'b1), .clk(CLK), .clr(RESET));  // open: carry
  Shifter #(.shift("lr"), .width(16)) shifter_1 (.in({D, {8{1'b0}}}), .\dist (multiplexer_1_out), .out(shifter_1_out));
  assign and_1_out = multiplexer_2_out & Q16;  // AND_Gate and_1, 16 bits wide
  assign D16 = shifter_1_out | and_1_out;  // OR_Gate or_1, 16 bits wide
  Multiplexer #(.width(8)) multiplexer_3 (.in0(Q16[7:0]), .in1(Q16[15:8]), .out(Q), .sel(BS));

  // Other names for the same wires on the sheet: D8[7:0] = D; high = BS; Q8[7:0] = Q
endmodule

module alu (
  input  WE,
  input  [15:0] A,
  input  [15:0] B,
  input  BS,
  input  [2:0] CMD,
  input  CLK,
  output [7:0] Q,
  output Z,
  output C
);

  wire adc, comparator_1_eq, multiplexer_2_out, sbc;
  wire [15:0] adder_1_out, and_1_out, divider_1_out, multiplexer_1_out, multiplier_1_out, or_1_out,
       register_1_q, shifter_1_out, shifter_2_out, subtractor_1_out, xor_1_out;

  Shifter #(.width(16)) shifter_1 (.in(A), .\dist (B[3:0]), .out(shifter_1_out));
  Adder #(.width(16)) adder_1 (.a(A), .b(B), .out(adder_1_out), .cin(1'b0), .cout(adc));
  Subtractor #(.width(16)) subtractor_1 (.a(A), .b(B), .out(subtractor_1_out), .bin(1'b0), .bout(sbc));
  Multiplier #(.width(16)) multiplier_1 (.a(A), .b(B), .out(multiplier_1_out), .cin({16{1'b0}}));  // open: cout
  Divider #(.width(16)) divider_1 (.a(A), .b(B), .out(divider_1_out), .upper({16{1'b0}}));  // open: rem
  assign and_1_out = A & B;  // AND_Gate and_1, 16 bits wide
  assign or_1_out = A | B;  // OR_Gate or_1, 16 bits wide
  assign xor_1_out = A ^ B;  // XOR_Gate xor_1, 16 bits wide
  Shifter #(.shift("lr"), .width(16)) shifter_2 (.in(shifter_1_out), .\dist (B[7:4]), .out(shifter_2_out));
  Multiplexer #(.select(3), .width(16)) multiplexer_1 (
    .in0(adder_1_out), .in1(subtractor_1_out), .in2(multiplier_1_out), .in3(divider_1_out), .in4(and_1_out),
    .in5(or_1_out), .in6(xor_1_out), .in7(shifter_2_out), .out(multiplexer_1_out), .sel(CMD));
  Register #(.trigger("high"), .width(16)) register_1 (
    .D(multiplexer_1_out), .clk(CLK), .Q(register_1_q));  // open: en, clr
  // Probe on multiplexer_1_out
  Multiplexer #(.select(3)) multiplexer_2 (
    .in0(adc), .in1(sbc), .in2(1'b0), .in3(1'b0), .in4(1'b0), .in5(1'b0), .in6(1'b0), .in7(1'b0),
    .out(multiplexer_2_out), .sel(CMD));
  Comparator #(.mode("unsigned"), .width(16)) comparator_1 (
    .a(multiplexer_1_out), .b({16{1'b0}}), .eq(comparator_1_eq));  // open: gt, lt
  D_Flip_Flop #(.trigger("falling")) IS_ZERO (.D(comparator_1_eq), .clk(WE), .Q(Z));  // open: Qn, preset, reset
  D_Flip_Flop DID_CARRY (.D(multiplexer_2_out), .clk(WE), .Q(C));  // open: Qn, preset, reset
  Multiplexer #(.width(8)) multiplexer_3 (.in0(register_1_q[7:0]), .in1(register_1_q[15:8]), .out(Q), .sel(BS));

  // Other names for the same wires on the sheet: A_16[15:0] = A; B_16[15:0] = B; byte_select = BS; latch = WE;
  //   Q8[7:0] = Q

  // Notes on the sheet:
  //   TODO: Add flags register
endmodule

module reg_16_8 (
  output [7:0] Q
);

  wire high;
  wire [15:0] Q16;

  Multiplexer #(.width(8)) multiplexer_1 (.in0(Q16[7:0]), .in1(Q16[15:8]), .out(Q), .sel(high));

  // Other names for the same wires on the sheet: Q8[7:0] = Q
endmodule
